// Logisim project project2CPU.circ as structural Verilog: 4 circuits, main circuit RegisterFile
module ALU (
  input  [7:0] input1,
  input  [7:0] input2,
  input  operation,
  output [7:0] ALUoutput
);

  wire [7:0] adder_1_out, subtractor_1_out;

  Adder adder_1 (.a(input1), .b(input2), .out(adder_1_out));  // open: cin, cout
  Subtractor subtractor_1 (.a(input2), .b(input1), .out(subtractor_1_out));  // open: bin, bout
  Multiplexer #(.width(8)) multiplexer_1 (.in0(adder_1_out), .in1(subtractor_1_out), .out(ALUoutput), .sel(operation));

  // Notes on the sheet:
  //   Does the computations for Additition and Subtraction instructions
endmodule

module RegisterFile (
  input  Clocky,
  input  [1:0] ReadReg1,
  input  [1:0] ReadReg2,
  input  [1:0] WriteReg,
  input  RegWrite,
  input  [7:0] RegDataW,
  output [7:0] RegData1,
  output [7:0] RegData2
);

  wire decoder_1_out0, decoder_1_out1, decoder_1_out2, decoder_1_out3, undriven, X1_out, X2_out, X3_out,
       X4_out;
  wire [7:0] register_1_q, register_2_q, register_3_q, register_4_q;

  Decoder #(.select(2)) decoder_1 (
    .out0(decoder_1_out0), .out1(decoder_1_out1), .out2(decoder_1_out2), .out3(decoder_1_out3),
    .sel(WriteReg), .en(undriven));
  and X1 (X1_out, RegWrite, decoder_1_out0);
  and X2 (X2_out, RegWrite, decoder_1_out1);
  and X3 (X3_out, RegWrite, decoder_1_out2);
  and X4 (X4_out, RegWrite, decoder_1_out3);
  Register register_1 (.D(RegDataW), .en(X1_out), .clk(Clocky), .Q(register_1_q));  // open: clr
  Register register_2 (.D(RegDataW), .en(X2_out), .clk(Clocky), .Q(register_2_q));  // open: clr
  Register register_3 (.D(RegDataW), .en(X3_out), .clk(Clocky), .Q(register_3_q));  // open: clr
  Register register_4 (.D(RegDataW), .en(X4_out), .clk(Clocky), .Q(register_4_q));  // open: clr
  Multiplexer #(.select(2), .width(8)) multiplexer_1 (
    .in0(register_1_q), .in1(register_2_q), .in2(register_3_q), .in3(register_4_q), .out(RegData1),
    .sel(ReadReg1));
  Multiplexer #(.select(2), .width(8)) multiplexer_2 (
    .in0(register_1_q), .in1(register_2_q), .in2(register_3_q), .in3(register_4_q), .out(RegData2),
    .sel(ReadReg2));

  // Notes on the sheet:
  //   Holds the Read/Write Registters. There are four general purpose registers: X1, X2, X3, and X4
endmodule

module ControlUnit (
  input  [15:0] Instruction,
  output [1:0] Rt,
  output [1:0] Ra,
  output [1:0] Rb,
  output [7:0] imm8,
  output ALUsed,
  output op,
  output LDR_reg,
  output LDR_imm,
  output STR
);

  and and_1 (ALUsed, Instruction[10], ~Instruction[12]);  // AND_Gate
  and and_2 (LDR_reg, ~Instruction[10], ~Instruction[11], Instruction[12]);  // AND_Gate
  and and_3 (LDR_imm, ~Instruction[10], Instruction[11], ~Instruction[12]);  // AND_Gate
  and and_4 (STR, ~Instruction[10], Instruction[11], Instruction[12]);  // AND_Gate

  assign imm8 = Instruction[9:2];
  assign op = Instruction[11];
  assign Ra = Instruction[3:2];
  assign Rb = Instruction[5:4];
  assign Rt = Instruction[1:0];

  // Notes on the sheet:
  //   This translates the opcode into different outputs ulitzied by the CPU
  //   - need 2 for second Reg
  //   - need 8 for 8-bit imm
  //   - need 2 for destination Reg
  //   - need 1 for arithmetic (0 = add, 1 = sub)
  //   -need 1 (mayb 2) for storing / loading
  //   LDR/STR = address + register
  //   Rt = the register an instruction is stored into
  //   imm8 = an immediate number, replaced Ra and Rb in instructions
  //   STR = 1 when storing data into a register
  //   ALUsed = 1 if an arithmetic instruction is being run
  //   op = 0 if addition, 1 if subtraction (assuming ALUsed = 1 too)
  //   LDR_reg = 1 when loading data using another register
  //   LDR_imm = 1 when loading data from an immediate
endmodule

// LDR_IMM
module CPU (
);

  wire ALUsed, Clocky, LDR, LDR_imm, opALU, or_1_out, STR;
  wire [1:0] inputA, inputB, target;
  wire [7:0] adder_1_out, alu_1_aluoutput, controlled_buffer_1_out, controlled_buffer_4_out, Data, immediate,
       register_1_q, registerfile_1_regdata1, registerfile_1_regdata2;
  wire [15:0] IR_q, rom_1_data;

  Register register_1 (.D(adder_1_out), .clk(Clocky), .Q(register_1_q));  // open: en, clr
  ROM #(.dataWidth(16)) rom_1 (.addr(register_1_q), .data(rom_1_data));
  Adder adder_1 (.a(register_1_q), .b(8'h1), .out(adder_1_out));  // open: cin, cout
  assign controlled_buffer_1_out = LDR_imm ? immediate : 8'bz;  // Controlled_Buffer controlled_buffer_1
  or or_1 (or_1_out, ALUsed, LDR, LDR_imm);
  Register #(.width(16)) IR (.D(rom_1_data), .clk(Clocky), .Q(IR_q));  // open: en, clr
  assign controlled_buffer_1_out = LDR ? Data : 8'bz;  // Controlled_Buffer controlled_buffer_2
  ControlUnit controlunit_1 (
    .Instruction(IR_q), .Rt(target), .Ra(inputA), .Rb(inputB), .imm8(immediate), .ALUsed(ALUsed), .op(opALU),
    .LDR_reg(LDR), .LDR_imm(LDR_imm), .STR(STR));
  RegisterFile registerfile_1 (
    .Clocky(Clocky), .ReadReg1(inputA), .ReadReg2(inputB), .WriteReg(target), .RegWrite(or_1_out),
    .RegDataW(controlled_buffer_1_out), .RegData1(registerfile_1_regdata1), .RegData2(registerfile_1_regdata2));
  assign controlled_buffer_1_out = ALUsed ? alu_1_aluoutput : 8'bz;  // Controlled_Buffer controlled_buffer_3
  assign controlled_buffer_4_out = STR ? registerfile_1_regdata1 : 8'bz;  // Controlled_Buffer controlled_buffer_4
  ALU alu_1 (
    .input1(registerfile_1_regdata1), .input2(registerfile_1_regdata2), .operation(opALU),
    .ALUoutput(alu_1_aluoutput));
  Clock clock_1 (.out(Clocky));
  RAM DataMemory (.addr(immediate), .we(STR), .oe(LDR), .clk(Clocky), .din(controlled_buffer_4_out), .dout(Data));

  // Notes on the sheet:
  //   PC
  //   contents of rom_1 (hex, n*v repeats v):
  //   804 1800 809 404 1002 81b c3b 404 1823
  //   instruction memory
  //   Names: James Schorle and Lucas Vanzelli
  //   CPU Name: Cuntina Pookie Unit (CPU)
  //   Pledge: I pledge my honor that I have abided by the Stevens Honor System.
  //   immediate also stores the address
endmodule
